# Fritzing sketch vezje_za_komponente_dopolnjen (saved by Fritzing 0.9.2b)
circuit board: 11.5486cm x 11.3745cm
circuit board: 1.5cm x 2.7cm
circuit board: 3.1cm x 5.8cm
circuit board: 4.5cm x 5cm
circuit board: 2.5cm x 4cm
circuit board: 2cm x 2.5cm
breadboards: 1

parts:
  Part2 = Arduino Nano (Rev3.0)
  Power_plug1 = Power plug
  J1 = female pin header, 15 pins [form="♀ (female)"]
  J2 = female pin header, 15 pins [form="♀ (female)"]
  C2 = Electrolytic Capacitor [capacitance=1µF package="100 mil [THT, electrolytic]"]
  IC1 = Voltage Regulator [package=to-220-alt]
  C3 = Electrolytic Capacitor [capacitance=1µF package="100 mil [THT, electrolytic]"]
  J3 = male pin header, 5 pins [form="♂ (male)"]
  J4 = male pin header, 4 pins [form="♂ (male)"]
  J5 = male pin header, 3 pins [form="♂ (male)"]
  J6 = male pin header, 4 pins [form="♂ (male)"]
  J7 = male pin header, 4 pins [form="♂ (male)"]
  R1 = Resistor [tolerance=±5% resistance=220 package=THT]
  U1 = LM358 [package=dip08]
  R2 = Resistor [tolerance=±5% resistance=220 package=THT]
  R3 = Resistor [tolerance=±5% resistance=220 package=THT]
  R4 = Resistor [tolerance=±5% resistance=220 package=THT]
  R5 = Resistor [tolerance=±5% resistance=220 package=THT]
  J8 = female pin header, 2 pins [form="♀ (female)"]
  C4 = Electrolytic Capacitor [capacitance=0.47mF package="200 mil [THT, electrolytic]"]
  R6 = Resistor [tolerance=±5% resistance=220 package=THT]

nets:
  N1: Part2.D1/TX, J1.pin4
  N2: Part2.D0/RX, J1.pin3
  GND: Part2.GND, Power_plug1.GND, J2.pin2, C2.-, IC1.GND, C3.-, J3.pin2, J4.pin1, J5.pin1, J6.pin1, J7.pin1, U1.G$1_V-, R2.Pin_1, J8.pin2
  N3: Part2.D2, J4.pin3, R1.Pin_1
  VIN: Part2.VIN, Power_plug1.VCC, J2.pin1, C2.+, IC1.IN
  N4: Part2.5V, J4.pin4, J5.pin2, J6.pin2, J7.pin2, R1.Pin_0, U1.G$1_V+, R3.Pin_1, R4.Pin_0
  N5: Part2.A7, J3.pin3
  N6: Part2.A6, U1.G$1_OUT, R6.Pin_1
  N7: Part2.A5, J7.pin4
  N8: Part2.A4, J7.pin3
  N9: Part2.A2, J6.pin4
  N10: Part2.A1, J6.pin3
  N11: Part2.A0, J5.pin3
  N12: IC1.OUT, C3.+, J3.pin5
  N13: U1.G$1_-IN, R5.Pin_0, R6.Pin_0
  N14: U1.G$1_+IN, R2.Pin_0, R3.Pin_0
  N15: R4.Pin_1, J8.pin1, C4.+
  N16: R5.Pin_1, C4.-
