# Fritzing sketch vezje_za_komponente_dopolnjen_pokoncni (saved by Fritzing 0.8.7b)
circuit board: 3.1cm x 5.8cm
circuit board: 3cm x 4cm
circuit board: 5.81cm x 25.0249cm
circuit board: 1.5cm x 2.7cm
circuit board: 4.5cm x 5cm
breadboards: 1

parts:
  ekran = Generic male header - 4 pins [form="♂ (male)" package=THT]
  U5 = LM358 [package=dip08]
  R24 = Resistor [tolerance=±5% resistance=220 package=THT]
  R25 = Resistor [tolerance=±5% resistance=220 package=THT]
  R26 = Resistor [tolerance=±5% resistance=220 package=THT]
  R27 = Resistor [tolerance=±5% resistance=220 package=THT]
  J40 = female pin header, 2 pins [form="♀ (female)"]
  A_nano = Arduino Nano (Rev3.0)
  zvok = Electrolytic Capacitor [capacitance=0.47mF package="200 mil [THT, electrolytic]"]
  R28 = Resistor [tolerance=±5% resistance=220 package=THT]
  IC8 = Voltage Regulator [package=to-220-alt]
  Power_plug7 = Power plug
  C20 = Electrolytic Capacitor [capacitance=1µF package="100 mil [THT, electrolytic]"]
  C21 = Electrolytic Capacitor [capacitance=1µF package="100 mil [THT, electrolytic]"]
  delci = Generic male header - 4 pins [form="♂ (male)" package=THT]
  Temperatura_in_vlaga = Generic male header - 4 pins [form="♂ (male)" package=THT]
  svetlost = Generic male header - 3 pins [form="♂ (male)" package=THT]
  WIFI = Generic female header - 15 pins [form="♀ (female)" package=THT]
  WIFI_2 = Generic female header - 15 pins [form="♀ (female)" package=THT]
  CO2 = Generic male header - 5 pins [form="♂ (male)" package=THT]
  R29 = Resistor [tolerance=±5% resistance=220 package=THT]

nets:
  N1: ekran.A#0, A_nano.A2
  N2: ekran.A#1, A_nano.A3
  5V: ekran.5V, U5.G$1_V+, A_nano.5V, delci.V, Temperatura_in_vlaga.5V, svetlost.V, R29.Pin_1
  GND: ekran.GND, U5.G$1_V-, R24.Pin_1, J40.pin2, A_nano.GND, IC8.GND, Power_plug7.GND, C20.-, C21.-, delci.GND, svetlost.GND, WIFI.GND, CO2.GND
  N3: U5.G$1_OUT, A_nano.A7, R28.Pin_1
  N4: U5.G$1_-IN, R26.Pin_0, R28.Pin_0
  N5: U5.G$1_+IN, R24.Pin_0, R25.Pin_0
  N6: R25.Pin_1, R27.Pin_0
  N7: R26.Pin_1, zvok.-
  N8: R27.Pin_1, J40.pin1, zvok.+
  N9: A_nano.D1/TX, WIFI_2.TX
  N10: A_nano.D0/RX, WIFI_2.RX
  N11: A_nano.D4, delci.D#1
  N12: A_nano.D5, delci.D#0
  VIN: A_nano.VIN, IC8.IN, Power_plug7.VCC, C21.+, WIFI.VIN
  N13: A_nano.A6, svetlost.A
  N14: A_nano.A1, Temperatura_in_vlaga.D, R29.Pin_0
  N15: A_nano.A0, CO2.A
  N16: C20.+, CO2.V

custom parts:
  Generic male header - 4 pins: Generic male header
  Generic male header - 4 pins: Generic male header
  Generic male header - 4 pins: Generic male header
  Generic male header - 3 pins: Generic male header
  Generic female header - 15 pins: Generic female header
  Generic female header - 15 pins: Generic female header
  Generic male header - 5 pins: Generic male header
